# Fritzing sketch rfid (saved by Fritzing 0.4.3b)

parts:
  Arduino1 = Arduino
  J1 = Basic Servo
  Parallax_RFID_Reader1 = RFID Reader

nets:
  N1: Arduino1.D9, Parallax_RFID_Reader1.connector1
  N2: Arduino1.D8, Parallax_RFID_Reader1.connector2
  N3: Arduino1.D3, J1.pulse
  N4: Arduino1.+5V, Parallax_RFID_Reader1.connector0
  GND: Arduino1.GND, J1.gnd, Parallax_RFID_Reader1.connector3
  VIN: Arduino1.VIN, J1.vcc
